// Logisim project alu.circ as structural Verilog: 16 circuits, main circuit add
module main (
  input  [15:0] X,
  input  [15:0] Y,
  input  [3:0] Switch__S,
  output Signed_Overflow,
  output [15:0] RESULT,
  output Equal
);

  wire Over_add, Over_addp8, Over_sub, Over_subp8;
  wire [15:0] add, addp8, \and , lui, \or , sllv, slt, srav, srlv, sub, subp8;

  add add_1 (.X(X), .Y(Y), .Overflow(Over_add), .Result(add));
  sub sub_1 (.X(X), .Y(Y), .Overflow(Over_sub), .Result(sub));
  sllv sllv_1 (.X(X), .Y(Y), .Result(sllv));
  srlv srlv_1 (.X(X), .Y(Y), .Result(srlv));
  srav srav_1 (.X(X), .Y(Y), .Result(srav));
  slt slt_1 (.X(X), .Y(Y), .Result(slt));
  \or  or_1 (.X(X), .Y(Y), .Result(\or ));
  \and  and_1 (.X(X), .Y(Y), .Result(\and ));
  addp8 addp8_1 (.X(X), .Y(Y), .Result(addp8), .Overflow(Over_addp8));
  subp8 subp8_1 (.X(X), .Y(Y), .Result(subp8), .Overflow(Over_subp8));
  Comparator #(.width(16)) comparator_1 (.a(X), .b(Y), .eq(Equal));  // open: gt, lt
  lui lui_1 (.Y(Y), .Result(lui));
  Multiplexer #(.select(4), .enable("false")) multiplexer_1 (
    .in0(Over_add), .in1(Over_sub), .in2(1'b0), .in3(1'b0), .in4(1'b0), .in5(1'b0), .in6(1'b0), .in7(1'b0),
    .in8(Over_addp8), .in9(Over_subp8), .in10(1'b0), .in11(1'b0), .in12(1'b0), .in13(1'b0), .in14(1'b0),
    .in15(1'b0), .out(Signed_Overflow), .sel(Switch__S));
  Multiplexer #(.select(4), .width(16), .enable("false")) multiplexer_2 (
    .in0(add), .in1(sub), .in2(sllv), .in3(srlv), .in4(srav), .in5(slt), .in6(\or ), .in7(\and ),
    .in8(addp8), .in9(subp8), .in10(lui), .out(RESULT), .sel(Switch__S));  // open: in11, in12, in13, in14, in15

  // Other names for the same wires on the sheet: S[3:0] = Switch__S; tunnel = Equal

  // Notes on the sheet:
  //   INPUTS to your circuit
  //   INPUT to your circuit
  //   DON'T CHANGE THE INPUTS AND OUTPUTS! IF YOU DO SO, YOU NEED TO MAKE SURE THE PINS ARE IN THE RIGHT PLACES!
  //   OUTPUTS of your circuit
endmodule

module add (
  input  [15:0] X,
  input  [15:0] Y,
  output Overflow,
  output [15:0] Result
);

  Adder #(.width(16)) adder_1 (.a(X), .b(Y), .out(Result));  // open: cin, cout
  overflow16_add overflow16_add (.X(X), .Y(Y), .Result(Result), .Overflow(Overflow));
endmodule

module sub (
  input  [15:0] X,
  input  [15:0] Y,
  output Overflow,
  output [15:0] Result
);

  Subtractor #(.width(16)) subtractor_1 (.a(X), .b(Y), .out(Result));  // open: bin, bout
  overflow16_sub overflow16_sub (.X(X), .Y(Y), .Result(Result), .Overflow(Overflow));
endmodule

module sllv (
  input  [15:0] X,
  input  [15:0] Y,
  output [15:0] Result
);

  wire [3:0] bit_extender_1_out;

  Bit_Extender #(.in_width(16), .out_width(4)) bit_extender_1 (.in(Y), .out(bit_extender_1_out));
  Shifter #(.width(16)) shifter_1 (.in(X), .\dist (bit_extender_1_out), .out(Result));
endmodule

module srlv (
  input  [15:0] X,
  input  [15:0] Y,
  output [15:0] Result
);

  wire [3:0] bit_extender_1_out;

  Bit_Extender #(.in_width(16), .out_width(4)) bit_extender_1 (.in(Y), .out(bit_extender_1_out));
  Shifter #(.width(16), .shift("lr")) shifter_1 (.in(X), .\dist (bit_extender_1_out), .out(Result));
endmodule

module srav (
  input  [15:0] X,
  input  [15:0] Y,
  output [15:0] Result
);

  wire [3:0] bit_extender_1_out;

  Bit_Extender #(.in_width(16), .out_width(4), .\type ("sign")) bit_extender_1 (.in(Y), .out(bit_extender_1_out));
  Shifter #(.width(16), .shift("ar")) shifter_1 (.in(X), .\dist (bit_extender_1_out), .out(Result));
endmodule

module slt (
  input  [15:0] X,
  input  [15:0] Y,
  output [15:0] Result
);

  wire comparator_1_lt;

  Comparator #(.width(16)) comparator_1 (.a(X), .b(Y), .lt(comparator_1_lt));  // open: gt, eq
  assign Result = {{15{1'b0}}, comparator_1_lt};  // Bit_Extender bit_extender_1
endmodule

module \or  (
  input  [15:0] X,
  input  [15:0] Y,
  output [15:0] Result
);

  assign Result = X | Y;  // OR_Gate or_1, 16 bits wide
endmodule

module \and  (
  input  [15:0] X,
  input  [15:0] Y,
  output [15:0] Result
);

  assign Result = X & Y;  // AND_Gate and_1, 16 bits wide
endmodule

module addp8 (
  input  [15:0] X,
  input  [15:0] Y,
  output [15:0] Result,
  output Overflow
);

  wire Overflow_7_0, Overflow_15_8;

  Adder adder_1 (.a(X[7:0]), .b(Y[7:0]), .out(Result[7:0]));  // open: cin, cout
  Adder adder_2 (.a(X[15:8]), .b(Y[15:8]), .out(Result[15:8]));  // open: cin, cout
  overflow8_add overflow8_add (.X(X[7:0]), .Y(Y[7:0]), .Result(Result[7:0]), .Overflow(Overflow_7_0));
  overflow8_add overflow8_add_2 (.X(X[15:8]), .Y(Y[15:8]), .Result(Result[15:8]), .Overflow(Overflow_15_8));
  or or_1 (Overflow, Overflow_7_0, Overflow_15_8);
endmodule

module subp8 (
  input  [15:0] X,
  input  [15:0] Y,
  output [15:0] Result,
  output Overflow
);

  wire Overflow_7_0, Overflow_15_8;

  Subtractor subtractor_1 (.a(X[7:0]), .b(Y[7:0]), .out(Result[7:0]));  // open: bin, bout
  Subtractor subtractor_2 (.a(X[15:8]), .b(Y[15:8]), .out(Result[15:8]));  // open: bin, bout
  overflow8_sub overflow8_sub (.X(X[7:0]), .Y(Y[7:0]), .Result(Result[7:0]), .Overflow(Overflow_7_0));
  overflow8_sub overflow8_sub_2 (.X(X[15:8]), .Y(Y[15:8]), .Result(Result[15:8]), .Overflow(Overflow_15_8));
  or or_1 (Overflow, Overflow_7_0, Overflow_15_8);
endmodule

module overflow16_add (
  input  [15:0] X,
  input  [15:0] Y,
  input  [15:0] Result,
  output Overflow
);

  wire and_1_out, and_2_out, nor_1_out, nor_2_out, nor_3_out, or_1_out;

  and and_1 (and_1_out, X[15], Y[15]);
  nor nor_1 (nor_1_out, Y[15], X[15]);
  and and_2 (and_2_out, X[15], Result[15]);
  nor nor_2 (nor_2_out, Result[15], X[15]);
  or or_1 (or_1_out, and_1_out, nor_1_out);
  nor nor_3 (nor_3_out, and_2_out, nor_2_out);
  and and_3 (Overflow, or_1_out, nor_3_out);

  // Notes on the sheet:
  //   Note: overflow occurs when adding two positive numbers produces a negative sum, or vice versa.
  //   X-Y Check
  //   X-Out Check
endmodule

module overflow16_sub (
  input  [15:0] X,
  input  [15:0] Y,
  input  [15:0] Result,
  output Overflow
);

  wire and_1_out, and_2_out, nor_1_out, nor_2_out, nor_3_out, or_1_out;
  wire [15:0] not_1_out;

  assign not_1_out = ~X;  // NOT_Gate not_1, 16 bits wide
  and and_1 (and_1_out, not_1_out[15], Y[15]);
  nor nor_1 (nor_1_out, Y[15], not_1_out[15]);
  and and_2 (and_2_out, X[15], Result[15]);
  nor nor_2 (nor_2_out, Result[15], X[15]);
  or or_1 (or_1_out, and_1_out, nor_1_out);
  nor nor_3 (nor_3_out, and_2_out, nor_2_out);
  and and_3 (Overflow, or_1_out, nor_3_out);

  // Notes on the sheet:
  //   X-Y Check
  //   X-Out Check
endmodule

module overflow8_add (
  input  [7:0] X,
  input  [7:0] Y,
  input  [7:0] Result,
  output Overflow
);

  wire and_1_out, and_2_out, nor_1_out, nor_2_out, nor_3_out, or_1_out;

  and and_1 (and_1_out, X[7], Y[7]);
  nor nor_1 (nor_1_out, Y[7], X[7]);
  and and_2 (and_2_out, X[7], Result[7]);
  nor nor_2 (nor_2_out, Result[7], X[7]);
  or or_1 (or_1_out, and_1_out, nor_1_out);
  nor nor_3 (nor_3_out, and_2_out, nor_2_out);
  and and_3 (Overflow, or_1_out, nor_3_out);

  // Notes on the sheet:
  //   X-Y Check
  //   X-Out Check
endmodule

module overflow8_sub (
  input  [7:0] X,
  input  [7:0] Y,
  input  [7:0] Result,
  output Overflow
);

  wire and_1_out, and_2_out, nor_1_out, nor_2_out, nor_3_out, or_1_out;
  wire [7:0] not_1_out;

  assign not_1_out = ~X;  // NOT_Gate not_1, 8 bits wide
  and and_1 (and_1_out, not_1_out[7], Y[7]);
  nor nor_1 (nor_1_out, Y[7], not_1_out[7]);
  and and_2 (and_2_out, X[7], Result[7]);
  nor nor_2 (nor_2_out, Result[7], X[7]);
  or or_1 (or_1_out, and_1_out, nor_1_out);
  nor nor_3 (nor_3_out, and_2_out, nor_2_out);
  and and_3 (Overflow, or_1_out, nor_3_out);

  // Notes on the sheet:
  //   X-Y Check
  //   X-Out Check
endmodule

module lui (
  input  [15:0] Y,
  output [15:0] Result
);

  Shifter #(.width(16)) shifter_1 (.in(Y), .\dist (4'b1000), .out(Result));
endmodule
