// Logisim project cpu.circ as structural Verilog: 14 circuits, main circuit main
module main (
  input  [15:0] From_Instr_Mem,
  input  clk,
  input  Reset,
  output [15:0] r0,
  output [15:0] r1,
  output [15:0] r2,
  output [15:0] r3,
  output [15:0] Display_0,
  output [15:0] Display_1,
  output [15:0] To_Instr_Mem,
  output [15:0] Data_Mem_Data,
  output [15:0] Data_Mem_Addr,
  output Data_Mem_Write
);

  wire alusrc_1_alusrc, comparator_1_eq, Kill, main_2_signed_overflow, memtoreg_1_memtoreg, not_1_out,
       regwrite_1_regwrite, Zero;
  wire [1:0] rd, regdst_1_writereg, rs_t, rt;
  wire [3:0] alucontrol_1_s, opcode;
  wire [5:0] funct;
  wire [7:0] imm8;
  wire [11:0] targetAdd;
  wire [15:0] ALU_X, imm16, MemData, multiplexer_1_out, multiplexer_2_out, multiplexer_3_out, NextPC,
       register_1_q, WriteData;

  Register #(.width(16)) currPC (.D(NextPC), .Q(To_Instr_Mem), .clk(clk));  // open: en, clr
  Multiplexer #(.width(16), .enable("false")) multiplexer_1 (
    .in0(From_Instr_Mem), .in1(16'h6), .out(multiplexer_1_out), .sel(Kill));
  Register #(.width(16)) register_1 (.D(multiplexer_1_out), .Q(register_1_q), .clk(clk));  // open: en, clr
  Kill kill_1 (.opcode(opcode), .Zero(Zero), .Kill(Kill));
  InstructionSplit instructionsplit_1 (
    .Instruction(register_1_q), .opcode(opcode), .rs(rs_t), .rt(rt), .rd(rd), .funct(funct),
    .immediate(imm8), .target_address(targetAdd));
  RegDst regdst_1 (.rt(rt), .rd(rd), .opcode(opcode), .WriteReg(regdst_1_writereg));
  RegWrite regwrite_1 (.opcode(opcode), .RegWrite(regwrite_1_regwrite));
  Regfile_main main_1 (
    .Read_register_1(rs_t), .Read_register_2(rt), .write_register(regdst_1_writereg), .write_data(WriteData),
    .Reg_0_Value(r0), .Reg_1_Value(r1), .Reg_2_Value(r2), .Reg_3_Value(r3), .RegWrite(regwrite_1_regwrite),
    .clock(clk), .Read_Data_1(ALU_X), .Read_Data_2(Data_Mem_Data));
  NextPC nextpc_1 (
    .opcode(opcode), .Zero(Zero), .PC(To_Instr_Mem), .imm16(imm16), .targetAdd(targetAdd), .rs(ALU_X),
    .NextPC(NextPC));
  Extender extender_1 (.Immediate(imm8), .opcode(opcode), .imm(imm16));
  ALUSrc alusrc_1 (.opcode(opcode), .ALUSrc(alusrc_1_alusrc));
  alu_main main_2 (
    .Switch__S(alucontrol_1_s), .X(ALU_X), .Equal(Zero), .RESULT(Data_Mem_Addr),
    .Signed_Overflow(main_2_signed_overflow), .Y(multiplexer_2_out));
  Multiplexer #(.width(16)) multiplexer_2 (
    .in0(Data_Mem_Data), .in1(imm16), .out(multiplexer_2_out), .sel(alusrc_1_alusrc));  // open: en
  ALUControl alucontrol_1 (.opcode(opcode), .funct(funct), .S(alucontrol_1_s));
  assign MemData = Data_Mem_Write ? Data_Mem_Data : 16'bz;  // Controlled_Buffer controlled_buffer_1
  not not_1 (not_1_out, Data_Mem_Write);
  Hex_Digit_Display hex_digit_display_1 (.value(Display_0[15:12]));  // open: dp
  Hex_Digit_Display hex_digit_display_2 (.value(Display_0[11:8]));  // open: dp
  LED led_1 (.in(main_2_signed_overflow));
  RAM #(.addrWidth(16), .dataWidth(16)) ram_1 (
    .addr(Data_Mem_Addr), .data(MemData), .sel(1'b1), .clk(clk), .ld(not_1_out), .clr(Reset));
  MemWrite MemWrite (.opcode(opcode), .MemWrite(Data_Mem_Write));
  Hex_Digit_Display hex_digit_display_3 (.value(Display_0[7:4]));  // open: dp
  Hex_Digit_Display hex_digit_display_4 (.value(Display_0[3:0]));  // open: dp
  Hex_Digit_Display hex_digit_display_5 (.value(Display_1[15:12]));  // open: dp
  Display u_display_1 (.opcode(opcode), .rs(ALU_X), .imm16(imm16), .clk(clk), .d0(Display_0), .d1(Display_1));
  MemtoReg memtoreg_1 (.opcode(opcode), .MemToReg(memtoreg_1_memtoreg));
  Hex_Digit_Display hex_digit_display_6 (.value(Display_1[11:8]));  // open: dp
  Hex_Digit_Display hex_digit_display_7 (.value(Display_1[7:4]));  // open: dp
  Multiplexer #(.width(16)) multiplexer_3 (
    .in0(Data_Mem_Addr), .in1(MemData), .out(multiplexer_3_out), .sel(memtoreg_1_memtoreg));  // open: en
  Hex_Digit_Display hex_digit_display_8 (.value(Display_1[3:0]));  // open: dp
  Multiplexer #(.width(16)) multiplexer_4 (
    .in0(multiplexer_3_out), .in1(To_Instr_Mem), .out(WriteData), .sel(comparator_1_eq));  // open: en
  Comparator #(.width(4)) comparator_1 (.a(opcode), .b(4'b0001), .eq(comparator_1_eq));  // open: gt, lt

  // Other names for the same wires on the sheet: Address[15:0] = Data_Mem_Addr; rs[15:0] = ALU_X;
  //   d0[15:0] = Display_0; d1[15:0] = Display_1; ALU_Y[15:0] = Data_Mem_Data; DataIn[15:0] = Data_Mem_Data;
  //   MemWrite = Data_Mem_Write; PC[15:0] = To_Instr_Mem

  // Notes on the sheet:
  //   Store PC
  //   This is the instruction that you
  //   would receive as INPUT
  //   This is the current PC that you need to send as OUTPUT
  //   Kill
  //   Instruction Fetch
  //   FALTA bootstraping
  //   This is a CLK that is an INPUT driven from the harness.
  //   Remember, this circuit is loaded from the harness to be tested!
  //   DO NOT CHANGE THE LOCATIONS OF THE INPUTS OR OUTPUTS! IF YOU DO SO, YOU NEED TO MAKE SURE THE PINS ARE IN THE RIGHT PLACES!
  //   These are OUTPUTS of the circuit
  //   Next PC
  //   Execution
  //   Data Memory
  //   Display
  //   These are OUTPUTS of the circuit
  //   jal
endmodule

module InstructionSplit (
  input  [15:0] Instruction,
  output [3:0] opcode,
  output [1:0] rs,
  output [1:0] rt,
  output [1:0] rd,
  output [5:0] funct,
  output [7:0] immediate,
  output [11:0] target_address
);


  assign funct = Instruction[5:0];
  assign immediate = Instruction[7:0];
  assign opcode = Instruction[15:12];
  assign rd = Instruction[7:6];
  assign rs = Instruction[11:10];
  assign rt = Instruction[9:8];
  assign target_address = Instruction[11:0];
endmodule

module RegDst (
  input  [1:0] rt,
  input  [1:0] rd,
  input  [3:0] opcode,
  output [1:0] WriteReg
);

  Multiplexer #(.select(4), .width(2)) multiplexer_1 (
    .in0(rd), .in1(2'b11), .in2(2'b00), .in3(2'b00), .in4(2'b00), .in5(rt), .in6(rt), .in7(rt), .in8(2'b00),
    .in9(2'b00), .in10(rt), .in11(rt), .in12(2'b00), .out(WriteReg), .sel(opcode));  // open: in13, in14, in15, en

  // Notes on the sheet:
  //   jal
endmodule

module RegWrite (
  input  [3:0] opcode,
  output RegWrite
);

  Multiplexer #(.select(4)) multiplexer_1 (
    .in0(1'b1), .in1(1'b1), .in2(1'b0), .in3(1'b0), .in4(1'b0), .in5(1'b1), .in6(1'b1), .in7(1'b1),
    .in8(1'b0), .in9(1'b0), .in10(1'b1), .in11(1'b1), .in12(1'b0), .out(RegWrite), .sel(opcode));  // open: in13, in14, in15, en

  // Notes on the sheet:
  //   j, jr, beq, bne, sw, disp
endmodule

// Ext.
module Extender (
  input  [7:0] Immediate,
  input  [3:0] opcode,
  output [15:0] imm
);

  wire [15:0] bit_extender_1_out, bit_extender_2_out;

  assign bit_extender_1_out = {{8{1'b0}}, Immediate};  // Bit_Extender bit_extender_1
  assign bit_extender_2_out = {{8{Immediate[7]}}, Immediate};  // Bit_Extender bit_extender_2
  Multiplexer #(.select(4), .width(16)) multiplexer_1 (
    .in0(bit_extender_1_out), .in1(bit_extender_1_out), .in2(bit_extender_1_out), .in3(bit_extender_1_out),
    .in4(bit_extender_2_out), .in5(bit_extender_2_out), .in6(bit_extender_1_out), .in7(bit_extender_1_out),
    .in8(bit_extender_2_out), .in9(bit_extender_2_out), .in10(bit_extender_1_out), .in11(bit_extender_2_out),
    .in12(bit_extender_1_out), .out(imm), .sel(opcode));  // open: in13, in14, in15, en

  // Notes on the sheet:
  //   beq, addi, bne, sw, lw
endmodule

module ALUSrc (
  input  [3:0] opcode,
  output ALUSrc
);

  wire comparator_1_eq, comparator_2_eq, comparator_3_eq, or_1_out;

  Comparator #(.width(4)) comparator_1 (.a(opcode), .b(4'b0000), .eq(comparator_1_eq));  // open: gt, lt
  Comparator #(.width(4)) comparator_2 (.a(opcode), .b(4'b0100), .eq(comparator_2_eq));  // open: gt, lt
  Comparator #(.width(4)) comparator_3 (.a(opcode), .b(4'b1000), .eq(comparator_3_eq));  // open: gt, lt
  or or_1 (or_1_out, comparator_1_eq, comparator_2_eq, comparator_3_eq);
  not not_1 (ALUSrc, or_1_out);
endmodule

module ALUControl (
  input  [3:0] opcode,
  input  [5:0] funct,
  output [3:0] S
);

  wire [3:0] funct_t;

  Bit_Extender #(.in_width(6), .out_width(4)) bit_extender_1 (.in(funct), .out(funct_t));
  Multiplexer #(.select(4), .width(4)) multiplexer_1 (
    .in0(funct_t), .in5(4'b0000), .in6(4'b0111), .in7(4'b0110), .in9(4'b0000), .in11(4'b0000), .out(S),
    .sel(opcode));  // open: in1, in2, in3, in4, in8, in10, in12, in13, in14, in15, en
endmodule

module MemWrite (
  input  [3:0] opcode,
  output MemWrite
);

  Comparator #(.width(4)) comparator_1 (.a(4'b1001), .b(opcode), .eq(MemWrite));  // open: gt, lt

  // Notes on the sheet:
  //   sw
endmodule

// MemToReg
module MemtoReg (
  input  [3:0] opcode,
  output MemToReg
);

  Comparator #(.width(4)) comparator_1 (.a(4'b1011), .b(opcode), .eq(MemToReg));  // open: gt, lt

  // Notes on the sheet:
  //   lw
endmodule

module Display (
  input  [3:0] opcode,
  input  [15:0] rs,
  input  [15:0] imm16,
  input  clk,
  output [15:0] d0,
  output [15:0] d1
);

  wire and_1_out, and_2_out, comparator_1_eq, comparator_2_eq, DisplayControl, imm;

  Bit_Extender #(.in_width(16), .out_width(1)) bit_extender_1 (.in(imm16), .out(imm));
  Comparator #(.width(1)) comparator_1 (.a(imm), .b(1'b0), .eq(comparator_1_eq));  // open: gt, lt
  Comparator #(.width(1)) comparator_2 (.a(imm), .b(1'b1), .eq(comparator_2_eq));  // open: gt, lt
  Comparator #(.width(4)) comparator_3 (.a(4'b1100), .b(opcode), .eq(DisplayControl));  // open: gt, lt
  and and_1 (and_1_out, DisplayControl, comparator_1_eq);
  and and_2 (and_2_out, DisplayControl, comparator_2_eq);
  Register #(.width(16)) register_1 (.D(rs), .en(and_1_out), .Q(d0), .clk(clk));  // open: clr
  Register #(.width(16)) register_2 (.D(rs), .en(and_2_out), .Q(d1), .clk(clk));  // open: clr

  // Notes on the sheet:
  //   disp
endmodule

// beq
module Branch_beq (
  input  [3:0] opcode,
  output beq
);

  Comparator #(.width(4)) comparator_1 (.a(opcode), .b(4'b0100), .eq(beq));  // open: gt, lt
endmodule

// bne
module Branch_bne (
  input  [3:0] opcode,
  output bne
);

  Comparator #(.width(4)) comparator_1 (.a(opcode), .b(4'b1000), .eq(bne));  // open: gt, lt
endmodule

module NextPC (
  input  [3:0] opcode,
  input  Zero,
  input  [15:0] PC,
  input  [15:0] imm16,
  input  [11:0] targetAdd,
  input  [15:0] rs,
  output [15:0] NextPC
);

  wire beq, bne, branch_beq_1_beq, branch_bne_1_bne, not_1_out;
  wire [15:0] adder_1_out, adder_2_out, adder_3_out, adder_4_out, adder_5_out, and_3_out, bit_extender_1_out,
       multiplexer_1_out, multiplexer_2_out, or_1_out;

  Branch_beq branch_beq_1 (.opcode(opcode), .beq(branch_beq_1_beq));
  Branch_bne branch_bne_1 (.opcode(opcode), .bne(branch_bne_1_bne));
  not not_1 (not_1_out, Zero);
  and and_1 (beq, branch_beq_1_beq, Zero);
  and and_2 (bne, branch_bne_1_bne, not_1_out);
  Adder #(.width(16)) adder_1 (.a(PC), .b(imm16), .out(adder_1_out));  // open: cin, cout
  Adder #(.width(16)) adder_2 (.a(PC), .b(imm16), .out(adder_2_out));  // open: cin, cout
  Adder #(.width(16)) adder_3 (.a(16'h1), .b(PC), .out(adder_3_out));  // open: cin, cout
  assign and_3_out = PC & 16'hf000;  // AND_Gate and_3, 16 bits wide
  assign bit_extender_1_out = {{4{1'b0}}, targetAdd};  // Bit_Extender bit_extender_1
  Adder #(.width(16)) adder_4 (.a(PC), .b(16'h1), .out(adder_4_out));  // open: cin, cout
  Adder #(.width(16)) adder_5 (.a(PC), .b(16'h1), .out(adder_5_out));  // open: cin, cout
  assign or_1_out = and_3_out | bit_extender_1_out;  // OR_Gate or_1, 16 bits wide
  Multiplexer #(.width(16)) multiplexer_1 (
    .in0(adder_4_out), .in1(adder_1_out), .out(multiplexer_1_out), .sel(beq));  // open: en
  Multiplexer #(.width(16)) multiplexer_2 (
    .in0(adder_5_out), .in1(adder_2_out), .out(multiplexer_2_out), .sel(bne));  // open: en
  Multiplexer #(.select(4), .width(16)) multiplexer_3 (
    .in0(adder_3_out), .in1(or_1_out), .in2(or_1_out), .in3(rs), .in4(multiplexer_1_out), .in5(adder_3_out),
    .in6(adder_3_out), .in7(adder_3_out), .in8(multiplexer_2_out), .in9(adder_3_out), .in10(adder_3_out),
    .in11(adder_3_out), .in12(adder_3_out), .out(NextPC), .sel(opcode));  // open: in13, in14, in15, en

  // Notes on the sheet:
  //   Check Branch
  //   Next PC
  //   bne
  //   jal, j
  //   beq
  //   jr
endmodule

module Kill (
  input  [3:0] opcode,
  input  Zero,
  output Kill
);

  wire and_1_out, and_2_out, beq, bne, branch_beq_1_beq, branch_bne_1_bne, comparator_1_eq, comparator_2_eq,
       comparator_3_eq, comparator_4_eq, comparator_5_eq, not_1_out;

  Comparator #(.width(4)) comparator_1 (.a(opcode), .b(4'b0100), .eq(comparator_1_eq));  // open: gt, lt
  Comparator #(.width(4)) comparator_2 (.a(opcode), .b(4'b1000), .eq(comparator_2_eq));  // open: gt, lt
  Comparator #(.width(4)) comparator_3 (.a(opcode), .b(4'b0001), .eq(comparator_3_eq));  // open: gt, lt
  Comparator #(.width(4)) comparator_4 (.a(opcode), .b(4'b0010), .eq(comparator_4_eq));  // open: gt, lt
  Comparator #(.width(4)) comparator_5 (.a(opcode), .b(4'b0011), .eq(comparator_5_eq));  // open: gt, lt
  and and_1 (and_1_out, comparator_1_eq, beq);
  and and_2 (and_2_out, comparator_2_eq, bne);
  Branch_beq branch_beq_1 (.opcode(opcode), .beq(branch_beq_1_beq));
  Branch_bne branch_bne_1 (.opcode(opcode), .bne(branch_bne_1_bne));
  not not_1 (not_1_out, Zero);
  or or_1 (Kill, and_1_out, and_2_out, comparator_3_eq, comparator_4_eq, comparator_5_eq);
  and and_3 (beq, branch_beq_1_beq, Zero);
  and and_4 (bne, branch_bne_1_bne, not_1_out);

  // Notes on the sheet:
  //   beq
  //   bne
  //   jal
  //   j
  //   jr
  //   Check Branch
endmodule
